// Logisim project hw3-2.circ as structural Verilog: 1 circuit, main circuit main
module main (
  input  A,
  input  B,
  output out_3
);

  wire transistor_1_out, transistor_2_out, transistor_5_out, transistor_8_out, transistor_9_out;

  Transistor transistor_1 (.in(1'b1), .out(transistor_1_out), .gate(A));
  Transistor transistor_2 (.in(1'b1), .out(transistor_2_out), .gate(B));
  Transistor #(.\type ("n")) transistor_3 (.in(1'b0), .out(transistor_2_out), .gate(B));
  Transistor #(.\type ("n")) transistor_4 (.in(1'b0), .out(transistor_1_out), .gate(A));
  Transistor transistor_5 (.in(1'b1), .out(transistor_5_out), .gate(transistor_1_out));
  Transistor transistor_6 (.in(transistor_5_out), .out(out_3), .gate(transistor_2_out));
  Transistor #(.\type ("n")) transistor_7 (.in(transistor_8_out), .out(out_3), .gate(A));
  Transistor #(.\type ("n")) transistor_8 (.in(1'b0), .out(transistor_8_out), .gate(transistor_1_out));
  Transistor transistor_9 (.in(1'b1), .out(transistor_9_out), .gate(A));
  Transistor transistor_10 (.in(transistor_9_out), .out(out_3), .gate(B));
  Transistor #(.\type ("n")) transistor_11 (.in(transistor_8_out), .out(out_3), .gate(B));
  Transistor #(.\type ("n")) transistor_12 (.in(1'b0), .out(transistor_8_out), .gate(transistor_2_out));

  // Notes on the sheet:
  //   CMSC 313 Homework 3, #2
endmodule
