// Logisim project 2-bit ALU.circ as structural Verilog: 1 circuit, main circuit main
module main (
  input  f0,
  input  B0,
  input  B1,
  input  A0,
  input  A1,
  input  f1,
  output overflow,
  output C0,
  output C1
);

  wire and_1_out, and_2_out, and_3_out, and_4_out, and_5_out, and_6_out, and_7_out, and_8_out, and_9_out,
       and_10_out, and_11_out, and_12_out, and_13_out, and_14_out, and_15_out, and_16_out, and_17_out,
       not_1_out, not_2_out, or_1_out, or_3_out, xor_1_out, xor_2_out, xor_3_out;

  and and_1 (and_1_out, f1, f0);
  and and_2 (and_2_out, f1, ~f0);  // AND_Gate
  and and_3 (and_3_out, ~f1, f0);  // AND_Gate
  and and_4 (and_4_out, ~f1, ~f0);  // AND_Gate
  and and_5 (and_5_out, B0, A0);
  and and_6 (and_6_out, and_5_out, and_1_out);
  not not_1 (not_1_out, A0);
  or or_1 (or_1_out, B0, A0);
  and and_7 (and_7_out, not_1_out, and_2_out);
  and and_8 (and_8_out, or_1_out, and_3_out);
  or or_2 (C0, and_6_out, and_7_out, and_8_out, and_9_out);
  xor xor_1 (xor_1_out, B0, A0);
  and and_9 (and_9_out, xor_1_out, and_4_out);
  and and_10 (and_10_out, B1, A1);
  and and_11 (and_11_out, and_10_out, and_1_out);
  and and_12 (and_12_out, B0, A0, and_4_out);
  or or_3 (or_3_out, B1, A1);
  not not_2 (not_2_out, A1);
  and and_13 (and_13_out, not_2_out, and_2_out);
  and and_14 (and_14_out, or_3_out, and_3_out);
  or or_4 (C1, and_11_out, and_13_out, and_14_out, and_15_out);
  xor xor_2 (xor_2_out, B1, A1);
  xor xor_3 (xor_3_out, and_12_out, xor_2_out);
  and and_15 (and_15_out, xor_3_out, and_4_out);
  and and_16 (and_16_out, B1, A1, and_4_out);
  or or_5 (overflow, and_16_out, and_17_out);
  and and_17 (and_17_out, and_4_out, xor_2_out, and_12_out);

  // Notes on the sheet:
  //   Instructions:
  //   decoder
  //   00 =ADD
  //   01 = NOT A
  //   10 = A OR B
  //   11 = A AND B
  //   carry
  //   half-adder
  //   full-adder
  //   A 2-bit
  //   Arithmetic Logic Unit
  //   (ALU)
endmodule
