// Logisim project 4-1 DEMUX.circ as structural Verilog: 1 circuit, main circuit main
module main (
  input  Input,
  input  S1,
  input  S0,
  output O0,
  output O1,
  output O2,
  output O3
);

  wire not_1_out, not_2_out;

  not not_1 (not_1_out, S1);
  not not_2 (not_2_out, S0);
  and and_1 (O0, not_1_out, not_2_out, Input);
  and and_2 (O1, not_1_out, S0, Input);
  and and_3 (O2, S1, not_2_out, Input);
  and and_4 (O3, S1, S0, Input);

  // Notes on the sheet:
  //   4-1 DEMUX
endmodule
