// Logisim project 4-1 MUX.circ as structural Verilog: 1 circuit, main circuit main
module main (
  input  I0,
  input  I1,
  input  I2,
  input  I3,
  input  S1,
  input  S0,
  output Output
);

  wire and_1_out, and_2_out, and_3_out, and_4_out, not_1_out, not_2_out;

  not not_1 (not_1_out, S1);
  not not_2 (not_2_out, S0);
  and and_1 (and_1_out, not_1_out, not_2_out, I0);
  and and_2 (and_2_out, not_1_out, S0, I1);
  and and_3 (and_3_out, S1, not_2_out, I2);
  and and_4 (and_4_out, S1, S0, I3);
  or or_1 (Output, and_1_out, and_2_out, and_3_out, and_4_out);

  // Notes on the sheet:
  //   4-1 MUX
endmodule
