// Logisim project Combined Adder-Subtractor.circ as structural Verilog: 2 circuits, main circuit main
module main (
  input  a3,
  input  a2,
  input  a1,
  input  a0,
  input  b3,
  input  b2,
  input  b1,
  input  b0,
  input  add_sub,
  output c_out,
  output s3,
  output s2,
  output s1,
  output s0
);

  wire full_adder_2_cout, full_adder_3_cout, full_adder_4_cout, xor_1_out, xor_2_out, xor_3_out, xor_4_out;

  xor xor_1 (xor_1_out, b3, add_sub);
  Full_Adder full_adder_1 (.cin(full_adder_2_cout), .x(a3), .y(xor_1_out), .Sum(s3), .cout(c_out));
  xor xor_2 (xor_2_out, b2, add_sub);
  Full_Adder full_adder_2 (.cin(full_adder_3_cout), .x(a2), .y(xor_2_out), .Sum(s2), .cout(full_adder_2_cout));
  xor xor_3 (xor_3_out, b1, add_sub);
  Full_Adder full_adder_3 (.cin(full_adder_4_cout), .x(a1), .y(xor_3_out), .Sum(s1), .cout(full_adder_3_cout));
  xor xor_4 (xor_4_out, b0, add_sub);
  Full_Adder full_adder_4 (.cin(add_sub), .x(a0), .y(xor_4_out), .Sum(s0), .cout(full_adder_4_cout));

  // Notes on the sheet:
  //   Combined Adder/Subtractor
endmodule

module Full_Adder (
  input  cin,
  input  x,
  input  y,
  output Sum,
  output cout
);

  wire and_1_out, and_2_out, xor_1_out;

  and and_1 (and_1_out, x, y);
  xor xor_1 (xor_1_out, x, y);
  and and_2 (and_2_out, cin, xor_1_out);
  xor xor_2 (Sum, cin, xor_1_out);
  or or_1 (cout, and_2_out, and_1_out);

  // Notes on the sheet:
  //   Full Adder
endmodule
