// Logisim project Full Adder.circ as structural Verilog: 1 circuit, main circuit main
module main (
  input  in_1,
  input  in_2,
  input  in_3,
  output Sum,
  output Carry
);

  wire and_1_out, and_2_out, xor_1_out;

  and and_1 (and_1_out, in_2, in_3);
  xor xor_1 (xor_1_out, in_2, in_3);
  and and_2 (and_2_out, in_1, xor_1_out);
  xor xor_2 (Sum, in_1, xor_1_out);
  or or_1 (Carry, and_2_out, and_1_out);

  // Notes on the sheet:
  //   Full Adder
endmodule
