// Logisim project Master Slave J-K Flip Flop.circ as structural Verilog: 1 circuit, main circuit main
module main (
);

  wire and_1_out, and_2_out, and_3_out, and_4_out, button_1_out, button_2_out, button_3_out, button_4_out,
       clock_1_out, nor_1_out, nor_2_out, nor_3_out, nor_4_out, not_1_out, or_1_out, or_2_out;

  Button button_1 (.out(button_1_out));
  Button button_2 (.out(button_2_out));
  Button button_3 (.out(button_3_out));
  or or_1 (or_1_out, button_1_out, button_2_out);
  or or_2 (or_2_out, button_2_out, button_3_out);
  Clock clock_1 (.out(clock_1_out));
  not not_1 (not_1_out, clock_1_out);
  and and_1 (and_1_out, nor_4_out, or_1_out, clock_1_out);
  and and_2 (and_2_out, clock_1_out, or_2_out, nor_3_out);
  Button button_4 (.out(button_4_out));
  nor nor_1 (nor_1_out, and_1_out, nor_2_out);
  nor nor_2 (nor_2_out, nor_1_out, and_2_out, button_4_out);
  and and_3 (and_3_out, not_1_out, nor_1_out);
  and and_4 (and_4_out, nor_2_out, not_1_out);
  nor nor_3 (nor_3_out, and_3_out, nor_4_out);
  nor nor_4 (nor_4_out, nor_3_out, and_4_out);
  LED led_1 (.in(nor_3_out));
  LED led_2 (.in(nor_4_out));

  // Notes on the sheet:
  //   Master-Slave J-K Flip Flop
  //   Set
  //   Toggle
  //   Reset
  //   Select "Reset Simulation" then press the "Clear" button to place the flip-flop in a consistent state.
  //   Clear
  //   Q
  //   ~Q
endmodule
