// Logisim project Negative Edge-Triggered D Flip-Flop.circ as structural Verilog: 1 circuit, main circuit main
module main (
  input  \input 
);

  wire _1_out, _2_out, _3_out, _4_out, _5_out, _6_out, clock_1_out;

  Clock clock_1 (.out(clock_1_out));
  nor _1 (_1_out, _4_out, _2_out);
  nor _2 (_2_out, _1_out, clock_1_out);
  nor _3 (_3_out, _2_out, clock_1_out, _4_out);
  nor _4 (_4_out, _3_out, \input );
  nor _5 (_5_out, _2_out, _6_out);
  nor _6 (_6_out, _5_out, _3_out);
  LED Q (.in(_5_out));
  LED nQ (.in(_6_out));

  // Notes on the sheet:
  //   Negative Edge-Triggered D Flip-Flop
  //   R
  //   S
endmodule
