// Logisim project NotNot.circ as structural Verilog: 1 circuit, main circuit main
module main (
  input  in_1,
  input  in_2,
  output out_3,
  output out_4
);

  wire not_1_out, transistor_1_out;

  Transistor transistor_1 (.in(1'b1), .out(transistor_1_out), .gate(in_1));
  Transistor #(.\type ("n")) transistor_2 (.in(1'b0), .out(transistor_1_out), .gate(in_1));
  not not_1 (not_1_out, in_2);
  Transistor transistor_3 (.in(1'b1), .out(in_1), .gate(transistor_1_out));
  Transistor #(.\type ("n")) transistor_4 (.in(1'b0), .out(in_1), .gate(transistor_1_out));
  not not_2 (in_2, not_1_out);

  assign out_3 = in_1;
  assign out_4 = in_2;
endmodule
