// Logisim project SR Flip-Flop.circ as structural Verilog: 1 circuit, main circuit main
module main (
);

  wire button_1_out, button_2_out, NOR_2_out, NOR_out;

  Button button_1 (.out(button_1_out));
  Button button_2 (.out(button_2_out));
  nor NOR (NOR_out, button_1_out, NOR_2_out);
  nor NOR_2 (NOR_2_out, NOR_out, button_2_out);
  LED led_1 (.in(NOR_out));
  LED led_2 (.in(NOR_2_out));

  // Notes on the sheet:
  //   Set
  //   Reset
  //   SR Latch
  //   ~Q
  //   Q
endmodule
