// Logisim project Mod 4 Counter (Moore).circ as structural Verilog: 1 circuit, main circuit main
module main (
  output q1,
  output q0
);

  wire and_1_out, and_2_out, and_3_out, and_4_out, clock_out, reset_out, s0_prime_out, s1_prime_out;

  Clock clock (.out(clock_out));
  Button reset (.out(reset_out));
  and and_1 (and_1_out, ~q0, ~q1, ~reset_out);  // AND_Gate
  and and_2 (and_2_out, ~q0, q1, ~reset_out);  // AND_Gate
  and and_3 (and_3_out, q0, ~q1, ~reset_out);  // AND_Gate
  and and_4 (and_4_out, ~q0, q1, ~reset_out);  // AND_Gate
  D_Flip_Flop s1 (.clk(clock_out), .D(s1_prime_out), .Q(q1));  // open: Qn, preset, en, reset
  or s0_prime (s0_prime_out, and_1_out, and_2_out);
  or s1_prime (s1_prime_out, and_3_out, and_4_out);
  D_Flip_Flop s0 (.clk(clock_out), .D(s0_prime_out), .Q(q0));  // open: Qn, preset, en, reset

  // Notes on the sheet:
  //   Mod 4 Counter (Moore)
  //   r s1 s0
endmodule
