// Logisim project Mod 4 Counter.circ as structural Verilog: 1 circuit, main circuit main
module main (
  output q0,
  output q1
);

  wire and_1_out, and_2_out, and_3_out, and_4_out, clock_out, reset_out, s0_q, s1_q;

  Clock clock (.out(clock_out));
  Button reset (.out(reset_out));
  and and_1 (and_1_out, ~s0_q, ~s1_q, ~reset_out);  // AND_Gate
  and and_2 (and_2_out, ~s0_q, s1_q, ~reset_out);  // AND_Gate
  and and_3 (and_3_out, s0_q, ~s1_q, ~reset_out);  // AND_Gate
  and and_4 (and_4_out, ~s0_q, s1_q, ~reset_out);  // AND_Gate
  D_Flip_Flop s1 (.clk(clock_out), .D(q1), .Q(s1_q));  // open: Qn, preset, en, reset
  or s0_prime (q0, and_1_out, and_2_out);
  or s1_prime (q1, and_3_out, and_4_out);
  D_Flip_Flop s0 (.clk(clock_out), .D(q0), .Q(s0_q));  // open: Qn, preset, en, reset

  // Notes on the sheet:
  //   Mod 4 Counter
  //   r s1 s0
endmodule
