// Logisim project Vending Machine (SOP).circ as structural Verilog: 1 circuit, main circuit main
module main (
  input  x1,
  input  x0,
  output z2,
  output z1,
  output z0
);

  wire _0_out, _1_out, _2_out, _4_out, _5_out, _6_out, _8_out, _9_out, _10_out, _12_out, _13_out, _14_out,
       clock_out, reset_out, s0_prime_out, s0_q, s1_prime_out, s1_q;

  Clock clock (.out(clock_out));
  Button reset (.out(reset_out));
  D_Flip_Flop s1 (.clk(clock_out), .D(s1_prime_out), .Q(s1_q), .reset(reset_out));  // open: Qn, preset, en
  and _0 (_0_out, ~x0, ~x1, ~s0_q, ~s1_q);  // AND_Gate
  and _1 (_1_out, x0, ~x1, ~s0_q, ~s1_q);  // AND_Gate
  and _2 (_2_out, ~x0, x1, ~s0_q, ~s1_q);  // AND_Gate
  and _4 (_4_out, ~x0, ~x1, s0_q, ~s1_q);  // AND_Gate
  and _5 (_5_out, x0, ~x1, s0_q, ~s1_q);  // AND_Gate
  and _6 (_6_out, ~x0, x1, s0_q, ~s1_q);  // AND_Gate
  and _8 (_8_out, ~x0, ~x1, ~s0_q, s1_q);  // AND_Gate
  and _9 (_9_out, x0, ~x1, ~s0_q, s1_q);  // AND_Gate
  and _10 (_10_out, ~x0, x1, ~s0_q, s1_q);  // AND_Gate
  and _12 (_12_out, ~x0, ~x1, s0_q, s1_q);  // AND_Gate
  and _13 (_13_out, x0, ~x1, s0_q, s1_q);  // AND_Gate
  and _14 (_14_out, ~x0, x1, s0_q, s1_q);  // AND_Gate
  D_Flip_Flop s0 (.clk(clock_out), .D(s0_prime_out), .Q(s0_q), .reset(reset_out));  // open: Qn, preset, en
  or s0_prime (s0_prime_out, _0_out, _5_out, _8_out, _14_out);
  or s1_prime (s1_prime_out, _1_out, _4_out, _5_out, _8_out);
  or u_z0 (z0, _6_out, _10_out, _14_out);
  or u_z1 (z1, _2_out, _10_out, _13_out, _14_out);
  or u_z2 (z2, _2_out, _6_out, _9_out, _10_out, _12_out, _13_out, _14_out);

  // Notes on the sheet:
  //   s1  s0 x1  x0
  //   432
  //   States (s1 s0):
  //   00 = A  (0cts)
  //   01 = B  (5cts)
  //   10 = C  (10cts)
  //   11 = D  (15cts)
  //   654
  //   098
  //   Input (x1 x0) :
  //   00 = nickel
  //   01 = dime
  //   10 = quarter
  //   11 = xxxx
  //   210
  //   Vending Machine (SOP)
  //   20 cents for gum
  //   nickel
  //   dispense
  //   change
  //   gum
  //   dime
  //   change
endmodule
