// Logisim project Vending Machine (buggy).circ as structural Verilog: 1 circuit, main circuit main
module main (
  input  x1,
  input  x0,
  output z2,
  output z1,
  output z0
);

  wire and_1_out, and_2_out, and_3_out, and_4_out, and_5_out, and_6_out, and_7_out, and_8_out, and_9_out,
       clock_out, or_1_out, or_2_out, or_3_out, reset_out, s0_prime_out, s0_q, s1_prime_out, s1_q;

  Clock clock (.out(clock_out));
  Button reset (.out(reset_out));
  D_Flip_Flop s1 (.clk(clock_out), .D(s1_prime_out), .Q(s1_q), .reset(reset_out));  // open: Qn, preset, en
  and and_1 (and_1_out, ~x0, ~x1, ~s0_q);  // AND_Gate
  and and_2 (and_2_out, x0, ~x1, s0_q, ~s1_q);  // AND_Gate
  and and_3 (and_3_out, ~x0, x1, s0_q, s1_q);  // AND_Gate
  and and_4 (and_4_out, x0, ~x1, ~s0_q, ~s1_q);  // AND_Gate
  and and_5 (and_5_out, ~x1, s0_q, ~s1_q);  // AND_Gate
  and and_6 (and_6_out, ~x0, ~x1, ~s0_q, s1_q);  // AND_Gate
  or or_1 (or_1_out, s0_q, s1_q);
  and and_7 (and_7_out, ~x0, x1, ~s1_q);  // AND_Gate
  and and_8 (and_8_out, x0, ~x1, s0_q, s1_q);  // AND_Gate
  and and_9 (and_9_out, ~x0, x1, s0_q, s1_q);  // AND_Gate
  or or_2 (or_2_out, x1, s1_q);
  or or_3 (or_3_out, x0, x1, s0_q);
  D_Flip_Flop s0 (.clk(clock_out), .D(s0_prime_out), .Q(s0_q), .reset(reset_out));  // open: Qn, preset, en
  or s0_prime (s0_prime_out, and_1_out, and_2_out, and_3_out);
  or s1_prime (s1_prime_out, and_4_out, and_5_out, and_6_out);
  and u_z0 (z0, ~x0, x1, or_1_out);  // AND_Gate
  or u_z1 (z1, and_7_out, and_8_out, and_9_out);
  and u_z2 (z2, or_2_out, or_3_out);

  // Notes on the sheet:
  //   s1  s0 x1  x0
  //   !!! BUGGY VERSION: CHECK STATE B WITH A QUARTER !!!
  //   Vending Machine
  //   20 cents for gum
  //   States (s1 s0):
  //   00 = A  (0cts)
  //   01 = B  (5cts)
  //   10 = C  (10cts)
  //   11 = D  (15cts)
  //   nickel
  //   dispense
  //   change
  //   gum
  //   Input (x1 x0) :
  //   00 = nickel
  //   01 = dime
  //   10 = quarter
  //   11 = xxxx
  //   dime
  //   change
endmodule
