// Logisim project Sequence Detector (JK flip flops).circ as structural Verilog: 1 circuit, main circuit main
module main (
  input  x,
  output z
);

  wire and_1_out, and_2_out, and_3_out, and_4_out, and_5_out, clock_out, not_1_out, not_2_out, or_1_out,
       reset_out, s0_q, s1_q, s2_q;

  Clock clock (.out(clock_out));
  Button reset (.out(reset_out));
  J_K_Flip_Flop s2 (.J(or_1_out), .clk(clock_out), .K(and_3_out), .Q(s2_q), .reset(reset_out));  // open: Qn, preset, en
  not not_1 (not_1_out, x);
  and and_1 (and_1_out, x, ~s0_q);  // AND_Gate
  not not_2 (not_2_out, x);
  or or_1 (or_1_out, s1_q, and_2_out);
  and and_2 (and_2_out, x, s0_q);
  and and_3 (and_3_out, ~x, s0_q);  // AND_Gate
  and and_4 (and_4_out, x, ~s1_q, s2_q);  // AND_Gate
  and and_5 (and_5_out, ~x, s1_q, s2_q);  // AND_Gate
  J_K_Flip_Flop s1 (
    .J(and_1_out), .clk(clock_out), .K(not_2_out), .Q(s1_q), .reset(reset_out));  // open: Qn, preset, en
  or u_z (z, and_4_out, and_5_out);
  J_K_Flip_Flop s0 (.J(not_1_out), .clk(clock_out), .K(x), .Q(s0_q), .reset(reset_out));  // open: Qn, preset, en

  // Notes on the sheet:
  //   Sequence Dectector (J-K flip flops)
  //   Output 1 when EXACTLY two of last three bits are 1
endmodule
