// Logisim project Sequence Detector (fixed).circ as structural Verilog: 1 circuit, main circuit main
module main (
  input  x,
  output z
);

  wire and_1_out, and_2_out, button_1_out, clock_1_out, or_1_out, or_2_out, or_3_out, s0_prime_out, s0_q,
       s1_prime_out, s1_q, s2_prime_out, s2_q;

  Clock clock_1 (.out(clock_1_out));
  Button button_1 (.out(button_1_out));
  not s0_prime (s0_prime_out, x);
  or or_1 (or_1_out, s0_q, s1_q, s2_q);
  or or_2 (or_2_out, x, ~s0_q, s2_q);  // OR_Gate
  or or_3 (or_3_out, x, ~s0_q, s1_q);  // OR_Gate
  D_Flip_Flop s2 (.clk(clock_1_out), .D(s2_prime_out), .Q(s2_q), .reset(button_1_out));  // open: Qn, preset, en
  xor s1_prime (s1_prime_out, x, s0_q);
  and s2_prime (s2_prime_out, or_1_out, or_2_out, or_3_out);
  and and_1 (and_1_out, ~x, ~s0_q, s1_q, s2_q);  // AND_Gate
  and and_2 (and_2_out, x, ~s1_q, s2_q);  // AND_Gate
  D_Flip_Flop s1 (.clk(clock_1_out), .D(s1_prime_out), .Q(s1_q), .reset(button_1_out));  // open: Qn, preset, en
  or u_z (z, and_1_out, and_2_out);
  D_Flip_Flop s0 (.clk(clock_1_out), .D(s0_prime_out), .Q(s0_q), .reset(button_1_out));  // open: Qn, preset, en

  // Notes on the sheet:
  //   Output 1 when EXACTLY two of last three bits are 1
  //   s2 s1 s0 x
  //   Sequence Dectector
endmodule
