// Logisim project 2-bit CPU v1.circ as structural Verilog: 2 circuits, main circuit main
module main (
  input  in_1,
  input  in_2,
  output cout
);

  wire clock_1_out, d_ff_1_q, d_ff_2_q, d_ff_3_q, d_ff_4_q, n2_bit_alu_1_d0, n2_bit_alu_1_d1, undriven,
       undriven_2;

  Clock clock_1 (.out(clock_1_out));
  D_Flip_Flop d_ff_1 (.clk(clock_1_out), .D(n2_bit_alu_1_d1), .Q(d_ff_1_q));  // open: Qn, preset, en, reset
  D_Flip_Flop d_ff_2 (.clk(clock_1_out), .D(n2_bit_alu_1_d0), .Q(d_ff_2_q));  // open: Qn, preset, en, reset
  _2_bit_ALU u_2_bit_alu_1 (
    .f0(in_2), .f1(in_1), .cout(cout), .B0(d_ff_4_q), .B1(d_ff_3_q), .A0(d_ff_2_q), .A1(d_ff_1_q),
    .D1(n2_bit_alu_1_d1), .D0(n2_bit_alu_1_d0));
  D_Flip_Flop d_ff_3 (.clk(clock_1_out), .D(undriven_2), .Q(d_ff_3_q));  // open: Qn, preset, en, reset
  D_Flip_Flop d_ff_4 (.clk(clock_1_out), .D(undriven), .Q(d_ff_4_q));  // open: Qn, preset, en, reset

  // Notes on the sheet:
  //   Instructions:
  //   00 = ADD A
  //   01 = A AND B
  //   10 = A OR B
  //   11 = NOT
  //   2-bit CPU, version 1
  //   Reg1
  //   A1 A0
  //   D1D0
  //   Reg0
  //   B1B0
  //   2-bit ALU
endmodule

module _2_bit_ALU (
  input  f0,
  input  A1,
  input  A0,
  input  B1,
  input  B0,
  input  f1,
  output cout,
  output D1,
  output D0
);

  wire and_1_out, and_2_out, and_3_out, and_4_out, and_5_out, and_6_out, and_7_out, and_8_out, and_9_out,
       and_10_out, and_11_out, and_12_out, and_13_out, and_14_out, and_15_out, and_16_out, and_17_out,
       not_1_out, not_2_out, or_2_out, or_4_out, xor_1_out, xor_2_out, xor_3_out;

  and and_1 (and_1_out, ~f0, ~f1);  // AND_Gate
  and and_2 (and_2_out, f0, ~f1);  // AND_Gate
  and and_3 (and_3_out, ~f0, f1);  // AND_Gate
  and and_4 (and_4_out, f0, f1);
  or or_1 (cout, and_5_out, and_6_out);
  and and_5 (and_5_out, and_1_out, B1, A1);
  xor xor_1 (xor_1_out, A1, B1);
  and and_6 (and_6_out, and_1_out, and_12_out, xor_1_out);
  xor xor_2 (xor_2_out, xor_1_out, and_12_out);
  and and_7 (and_7_out, A1, B1);
  or or_2 (or_2_out, A1, B1);
  and and_8 (and_8_out, and_7_out, and_2_out);
  and and_9 (and_9_out, xor_2_out, and_1_out);
  or or_3 (D1, and_9_out, and_8_out, and_11_out, and_10_out);
  not not_1 (not_1_out, A1);
  and and_10 (and_10_out, not_1_out, and_4_out);
  and and_11 (and_11_out, or_2_out, and_3_out);
  and and_12 (and_12_out, and_1_out, B0, A0);
  xor xor_3 (xor_3_out, A0, B0);
  and and_13 (and_13_out, xor_3_out, and_1_out);
  or or_4 (or_4_out, A0, B0);
  and and_14 (and_14_out, A0, B0);
  and and_15 (and_15_out, and_14_out, and_2_out);
  and and_16 (and_16_out, or_4_out, and_3_out);
  or or_5 (D0, and_13_out, and_15_out, and_16_out, and_17_out);
  not not_2 (not_2_out, A0);
  and and_17 (and_17_out, not_2_out, and_4_out);

  // Notes on the sheet:
  //   Instructions:
  //   00 = ADD A
  //   01 = A AND B
  //   10 = A OR B
  //   11 = NOT
  //   A 2-bit
  //   Arithmetic Logic Unit
  //   (ALU)
  //   decoder
  //   full-
  //   adder
  //   carry
  //   half-
  //   adder
endmodule
