// Logisim project 2-bit CPU v10.circ as structural Verilog: 6 circuits, main circuit main
module main (
  output cout
);

  wire clock_out, Instr__Decode_alu_instruction, Instr__Decode_dest_mux, Instr__Decode_out_2, reset_out;
  wire [1:0] d_ff_2_q, d_ff_4_q, demultiplexer_1_out0, demultiplexer_1_out1, Instr__Decode_alu_a,
       Instr__Decode_alu_b, Instr__Decode_imm, Instr__Decode_result_mux, multiplexer_1_out,
       multiplexer_2_out, multiplexer_3_out, n2_bit_alu_1_d0, undriven, undriven_2;
  wire [3:0] n4_bit_counter_1_out_3;
  wire [7:0] n8_x_16_bit_rom_1_data;

  Clock clock (.out(clock_out));
  Button reset (.out(reset_out));
  _4_bit_counter u_4_bit_counter_1 (.reset(reset_out), .out_3(n4_bit_counter_1_out_3), .clk(clock_out));
  // Probe on n4_bit_counter_1_out_3
  // Probe on n8_x_16_bit_rom_1_data
  _8_x_16_bit_ROM u_8_x_16_bit_rom_1 (.addr(n4_bit_counter_1_out_3), .data(n8_x_16_bit_rom_1_data));  // open: in_1
  Instruction_Decoder Instr__Decode (
    .in_1(n8_x_16_bit_rom_1_data), .out_2(Instr__Decode_out_2),
    .ALU_Instruction(Instr__Decode_alu_instruction), .ALU_A(Instr__Decode_alu_a),
    .ALU_B(Instr__Decode_alu_b), .imm(Instr__Decode_imm), .result_mux(Instr__Decode_result_mux),
    .dest_mux(Instr__Decode_dest_mux));
  D_Flip_Flop d_ff_1 (.clk(clock_out), .D(demultiplexer_1_out1[1]), .Q(d_ff_2_q[1]));  // open: Qn, preset, en, reset
  D_Flip_Flop d_ff_2 (.clk(clock_out), .D(demultiplexer_1_out1[0]), .Q(d_ff_2_q[0]));  // open: Qn, preset, en, reset
  Multiplexer #(.select(2), .width(2), .enable("false")) multiplexer_1 (
    .in0(d_ff_4_q), .in1(d_ff_2_q), .in2(Instr__Decode_imm), .in3(undriven), .out(multiplexer_1_out),
    .sel(Instr__Decode_alu_a));
  _2_bit_ALU u_2_bit_alu_1 (
    .f0(Instr__Decode_out_2), .f1(Instr__Decode_alu_instruction), .cout(cout), .B0(multiplexer_2_out[0]),
    .B1(multiplexer_2_out[1]), .A0(multiplexer_1_out[0]), .A1(multiplexer_1_out[1]), .D1(n2_bit_alu_1_d0[1]),
    .D0(n2_bit_alu_1_d0[0]));
  // Probe on Instr__Decode_alu_instruction
  Multiplexer #(.select(2), .width(2), .enable("false")) multiplexer_2 (
    .in0(d_ff_4_q), .in1(d_ff_2_q), .in2(Instr__Decode_imm), .in3(undriven_2), .out(multiplexer_2_out),
    .sel(Instr__Decode_alu_b));
  // Probe on Instr__Decode_alu_a
  // Probe on Instr__Decode_out_2
  D_Flip_Flop d_ff_3 (.clk(clock_out), .D(demultiplexer_1_out0[1]), .Q(d_ff_4_q[1]));  // open: Qn, preset, en, reset
  // Probe on Instr__Decode_imm
  // Probe on Instr__Decode_alu_b
  D_Flip_Flop d_ff_4 (.clk(clock_out), .D(demultiplexer_1_out0[0]), .Q(d_ff_4_q[0]));  // open: Qn, preset, en, reset
  Multiplexer #(.select(2), .width(2), .enable("false")) multiplexer_3 (
    .in0(d_ff_4_q), .in1(d_ff_2_q), .in2(Instr__Decode_imm), .in3(n2_bit_alu_1_d0), .out(multiplexer_3_out),
    .sel(Instr__Decode_result_mux));
  // Probe on Instr__Decode_result_mux
  Demultiplexer #(.width(2), .tristate("true"), .enable("false")) demultiplexer_1 (
    .out0(demultiplexer_1_out0), .out1(demultiplexer_1_out1), .in(multiplexer_3_out),
    .sel(Instr__Decode_dest_mux));
  // Probe on Instr__Decode_dest_mux

  // Notes on the sheet:
  //   4-bit counter
  //   Reg1
  //   Program ROM
  //   ALU Instructions:
  //   00 = ADD A
  //   01 = A AND B
  //   10 = A OR B
  //   11 = NOT
  //   A1 A0
  //   B1B0
  //   2-bit ALU
  //   D1D0
  //   ALU inst
  //   Reg0
  //   ALU A
  //   ALU MUX
  //   00=Reg0  01=Reg1
  //   10=imm  11=xx
  //   ALU B
  //   imm
  //   Res MUX
  //   RES MUX
  //   00=Reg0  01=Reg1
  //   10=imm  11=ALU
  //   dest
endmodule

module _2_bit_ALU (
  input  f0,
  input  A1,
  input  A0,
  input  B1,
  input  B0,
  input  f1,
  output cout,
  output D1,
  output D0
);

  wire and_1_out, and_2_out, and_3_out, and_4_out, and_5_out, and_6_out, and_7_out, and_8_out, and_9_out,
       and_10_out, and_11_out, and_12_out, and_13_out, and_14_out, and_15_out, and_16_out, and_17_out,
       not_1_out, not_2_out, or_2_out, or_4_out, xor_1_out, xor_2_out, xor_3_out;

  and and_1 (and_1_out, ~f0, ~f1);  // AND_Gate
  and and_2 (and_2_out, f0, ~f1);  // AND_Gate
  and and_3 (and_3_out, ~f0, f1);  // AND_Gate
  and and_4 (and_4_out, f0, f1);
  or or_1 (cout, and_5_out, and_6_out);
  and and_5 (and_5_out, and_1_out, B1, A1);
  xor xor_1 (xor_1_out, A1, B1);
  and and_6 (and_6_out, and_1_out, and_12_out, xor_1_out);
  xor xor_2 (xor_2_out, xor_1_out, and_12_out);
  or or_2 (or_2_out, A1, B1);
  and and_7 (and_7_out, A1, B1);
  and and_8 (and_8_out, and_7_out, and_2_out);
  and and_9 (and_9_out, xor_2_out, and_1_out);
  or or_3 (D1, and_9_out, and_8_out, and_10_out, and_11_out);
  not not_1 (not_1_out, A1);
  and and_10 (and_10_out, or_2_out, and_3_out);
  and and_11 (and_11_out, not_1_out, and_4_out);
  and and_12 (and_12_out, and_1_out, B0, A0);
  xor xor_3 (xor_3_out, A0, B0);
  and and_13 (and_13_out, xor_3_out, and_1_out);
  and and_14 (and_14_out, A0, B0);
  or or_4 (or_4_out, A0, B0);
  and and_15 (and_15_out, and_14_out, and_2_out);
  and and_16 (and_16_out, or_4_out, and_3_out);
  or or_5 (D0, and_13_out, and_15_out, and_16_out, and_17_out);
  not not_2 (not_2_out, A0);
  and and_17 (and_17_out, not_2_out, and_4_out);

  // Notes on the sheet:
  //   Instructions:
  //   00 = ADD A
  //   01 = A AND B
  //   10 = A OR B
  //   11 = NOT
  //   A 2-bit
  //   Arithmetic Logic Unit
  //   (ALU)
  //   decoder
  //   full-
  //   adder
  //   carry
  //   half-
  //   adder
endmodule

module Instruction_Decoder (
  input  [7:0] in_1,
  output out_2,
  output ALU_Instruction,
  output [1:0] ALU_A,
  output [1:0] ALU_B,
  output [1:0] imm,
  output [1:0] result_mux,
  output dest_mux
);

  wire and_2_out;

  and and_1 (ALU_B[0], ~in_1[3], in_1[2]);  // AND_Gate
  and and_2 (and_2_out, ~in_1[3], in_1[2]);  // AND_Gate
  or or_1 (result_mux[1], ~in_1[7], in_1[3]);  // OR_Gate
  or or_2 (result_mux[0], ~in_1[7], and_2_out);  // OR_Gate

  assign ALU_A = {1'b0, in_1[4]};
  assign ALU_B[1] = in_1[3];
  assign ALU_Instruction = in_1[6];
  assign dest_mux = in_1[0];
  assign imm = in_1[2:1];
  assign out_2 = in_1[5];

  // Notes on the sheet:
  //   Instruction Decoder
endmodule

module _4_bit_counter (
  input  clk,
  input  reset,
  output [3:0] out_3
);

  wire and_1_out, and_2_out, not_1_out, xor_1_out, xor_2_out, xor_3_out;

  D_Flip_Flop d_ff_1 (.clk(clk), .D(xor_3_out), .Q(out_3[3]), .reset(reset));  // open: Qn, preset, en
  and and_1 (and_1_out, out_3[0], out_3[1]);
  and and_2 (and_2_out, out_3[0], out_3[1], out_3[2]);
  D_Flip_Flop d_ff_2 (.clk(clk), .D(xor_2_out), .Q(out_3[2]), .reset(reset));  // open: Qn, preset, en
  not not_1 (not_1_out, out_3[0]);
  xor xor_1 (xor_1_out, out_3[0], out_3[1]);
  xor xor_2 (xor_2_out, and_1_out, out_3[2]);
  xor xor_3 (xor_3_out, and_2_out, out_3[3]);
  D_Flip_Flop d_ff_3 (.clk(clk), .D(xor_1_out), .Q(out_3[1]), .reset(reset));  // open: Qn, preset, en
  D_Flip_Flop d_ff_4 (.clk(clk), .D(not_1_out), .Q(out_3[0]), .reset(reset));  // open: Qn, preset, en
endmodule

module _8_x_16_bit_ROM (
  input  in_1,
  input  [3:0] addr,
  output [7:0] data
);

  _16_bit_ROM u_16_bit_rom_1 (.reset(in_1), .enbl(1'b1), .addr(addr), .data(data[7]));
  _16_bit_ROM u_16_bit_rom_2 (.reset(in_1), .enbl(1'b1), .addr(addr), .data(data[6]));
  _16_bit_ROM u_16_bit_rom_3 (.reset(in_1), .enbl(1'b1), .addr(addr), .data(data[5]));
  _16_bit_ROM u_16_bit_rom_4 (.reset(in_1), .enbl(1'b1), .addr(addr), .data(data[4]));
  _16_bit_ROM u_16_bit_rom_5 (.reset(in_1), .enbl(1'b1), .addr(addr), .data(data[3]));
  _16_bit_ROM u_16_bit_rom_6 (.reset(in_1), .enbl(1'b1), .addr(addr), .data(data[2]));
  _16_bit_ROM u_16_bit_rom_7 (.reset(in_1), .enbl(1'b1), .addr(addr), .data(data[1]));
  _16_bit_ROM u_16_bit_rom_8 (.reset(in_1), .enbl(1'b1), .addr(addr), .data(data[0]));

  // Notes on the sheet:
  //   8 x 16-bit ROM
endmodule

// 16x1-bit
module _16_bit_ROM (
  input  reset,
  input  enbl,
  input  [3:0] addr,
  output data
);

  wire controlled_buffer_1_out, controlled_buffer_5_out, controlled_buffer_9_out, controlled_buffer_13_out,
       d_ff_1_q, d_ff_2_q, d_ff_3_q, d_ff_4_q, d_ff_5_q, d_ff_6_q, d_ff_7_q, d_ff_8_q, d_ff_9_q, d_ff_10_q,
       d_ff_11_q, d_ff_12_q, d_ff_13_q, d_ff_14_q, d_ff_15_q, d_ff_16_q, decoder_1_out0, decoder_1_out1,
       decoder_1_out2, decoder_1_out3;

  Decoder #(.select(2), .disabled(0)) decoder_1 (
    .out0(decoder_1_out0), .out1(decoder_1_out1), .out2(decoder_1_out2), .out3(decoder_1_out3),
    .sel(addr[3:2]), .en(enbl));
  // Probe on addr[3:2]
  D_Flip_Flop d_ff_1 (.Q(d_ff_1_q), .en(decoder_1_out0), .reset(reset));  // open: clk, D, Qn, preset
  assign controlled_buffer_1_out = decoder_1_out0 ? d_ff_1_q : 1'bz;  // Controlled_Buffer controlled_buffer_1
  assign controlled_buffer_1_out = decoder_1_out1 ? d_ff_2_q : 1'bz;  // Controlled_Buffer controlled_buffer_2
  D_Flip_Flop d_ff_2 (.Q(d_ff_2_q), .en(decoder_1_out1), .reset(reset));  // open: clk, D, Qn, preset
  assign controlled_buffer_1_out = decoder_1_out2 ? d_ff_3_q : 1'bz;  // Controlled_Buffer controlled_buffer_3
  D_Flip_Flop d_ff_3 (.Q(d_ff_3_q), .en(decoder_1_out2), .reset(reset));  // open: clk, D, Qn, preset
  D_Flip_Flop d_ff_4 (.Q(d_ff_4_q), .en(decoder_1_out3), .reset(reset));  // open: clk, D, Qn, preset
  assign controlled_buffer_1_out = decoder_1_out3 ? d_ff_4_q : 1'bz;  // Controlled_Buffer controlled_buffer_4
  // Probe on addr[1:0]
  D_Flip_Flop d_ff_5 (.Q(d_ff_5_q), .en(decoder_1_out0), .reset(reset));  // open: clk, D, Qn, preset
  D_Flip_Flop d_ff_6 (.Q(d_ff_6_q), .en(decoder_1_out1), .reset(reset));  // open: clk, D, Qn, preset
  D_Flip_Flop d_ff_7 (.Q(d_ff_7_q), .en(decoder_1_out2), .reset(reset));  // open: clk, D, Qn, preset
  D_Flip_Flop d_ff_8 (.Q(d_ff_8_q), .en(decoder_1_out3), .reset(reset));  // open: clk, D, Qn, preset
  assign controlled_buffer_5_out = decoder_1_out0 ? d_ff_5_q : 1'bz;  // Controlled_Buffer controlled_buffer_5
  assign controlled_buffer_5_out = decoder_1_out1 ? d_ff_6_q : 1'bz;  // Controlled_Buffer controlled_buffer_6
  assign controlled_buffer_5_out = decoder_1_out2 ? d_ff_7_q : 1'bz;  // Controlled_Buffer controlled_buffer_7
  assign controlled_buffer_5_out = decoder_1_out3 ? d_ff_8_q : 1'bz;  // Controlled_Buffer controlled_buffer_8
  assign controlled_buffer_9_out = decoder_1_out0 ? d_ff_9_q : 1'bz;  // Controlled_Buffer controlled_buffer_9
  D_Flip_Flop d_ff_9 (.Q(d_ff_9_q), .en(decoder_1_out0), .reset(reset));  // open: clk, D, Qn, preset
  D_Flip_Flop d_ff_10 (.Q(d_ff_10_q), .en(decoder_1_out1), .reset(reset));  // open: clk, D, Qn, preset
  assign controlled_buffer_9_out = decoder_1_out1 ? d_ff_10_q : 1'bz;  // Controlled_Buffer controlled_buffer_10
  D_Flip_Flop d_ff_11 (.Q(d_ff_11_q), .en(decoder_1_out2), .reset(reset));  // open: clk, D, Qn, preset
  assign controlled_buffer_9_out = decoder_1_out2 ? d_ff_11_q : 1'bz;  // Controlled_Buffer controlled_buffer_11
  D_Flip_Flop d_ff_12 (.Q(d_ff_12_q), .en(decoder_1_out3), .reset(reset));  // open: clk, D, Qn, preset
  assign controlled_buffer_9_out = decoder_1_out3 ? d_ff_12_q : 1'bz;  // Controlled_Buffer controlled_buffer_12
  Multiplexer #(.select(2)) multiplexer_1 (
    .in0(controlled_buffer_1_out), .in1(controlled_buffer_5_out), .in2(controlled_buffer_9_out),
    .in3(controlled_buffer_13_out), .out(data), .sel(addr[1:0]), .en(enbl));
  D_Flip_Flop d_ff_13 (.Q(d_ff_13_q), .en(decoder_1_out0), .reset(reset));  // open: clk, D, Qn, preset
  assign controlled_buffer_13_out = decoder_1_out0 ? d_ff_13_q : 1'bz;  // Controlled_Buffer controlled_buffer_13
  D_Flip_Flop d_ff_14 (.Q(d_ff_14_q), .en(decoder_1_out1), .reset(reset));  // open: clk, D, Qn, preset
  assign controlled_buffer_13_out = decoder_1_out1 ? d_ff_14_q : 1'bz;  // Controlled_Buffer controlled_buffer_14
  assign controlled_buffer_13_out = decoder_1_out2 ? d_ff_15_q : 1'bz;  // Controlled_Buffer controlled_buffer_15
  D_Flip_Flop d_ff_15 (.Q(d_ff_15_q), .en(decoder_1_out2), .reset(reset));  // open: clk, D, Qn, preset
  D_Flip_Flop d_ff_16 (.Q(d_ff_16_q), .en(decoder_1_out3), .reset(reset));  // open: clk, D, Qn, preset
  assign controlled_buffer_13_out = decoder_1_out3 ? d_ff_16_q : 1'bz;  // Controlled_Buffer controlled_buffer_16

  // Notes on the sheet:
  //   16-bit ROM
endmodule
