// Logisim project 2-bit CPU v4.circ as structural Verilog: 2 circuits, main circuit main
module main (
  input  dest_reg,
  input  [1:0] imm_operand,
  input  [1:0] in_3,
  input  [1:0] in_4,
  input  ALU_inst,
  input  in_6,
  input  [1:0] result_source,
  output cout
);

  wire clock_1_out;
  wire [1:0] d_ff_2_q, d_ff_4_q, demultiplexer_1_out0, demultiplexer_1_out1, multiplexer_1_out,
       multiplexer_2_out, multiplexer_3_out, n2_bit_alu_1_d0, undriven, undriven_2;

  Clock clock_1 (.out(clock_1_out));
  D_Flip_Flop d_ff_1 (.clk(clock_1_out), .D(demultiplexer_1_out1[1]), .Q(d_ff_2_q[1]));  // open: Qn, preset, en, reset
  D_Flip_Flop d_ff_2 (.clk(clock_1_out), .D(demultiplexer_1_out1[0]), .Q(d_ff_2_q[0]));  // open: Qn, preset, en, reset
  Multiplexer #(.select(2), .width(2), .enable("false")) multiplexer_1 (
    .in0(d_ff_4_q), .in1(d_ff_2_q), .in2(imm_operand), .in3(undriven), .out(multiplexer_1_out), .sel(in_3));
  Multiplexer #(.select(2), .width(2), .enable("false")) multiplexer_2 (
    .in0(d_ff_4_q), .in1(d_ff_2_q), .in2(imm_operand), .in3(undriven_2), .out(multiplexer_2_out), .sel(in_4));
  _2_bit_ALU u_2_bit_alu_1 (
    .f0(in_6), .f1(ALU_inst), .cout(cout), .B0(multiplexer_2_out[0]), .B1(multiplexer_2_out[1]),
    .A0(multiplexer_1_out[0]), .A1(multiplexer_1_out[1]), .D1(n2_bit_alu_1_d0[1]), .D0(n2_bit_alu_1_d0[0]));
  D_Flip_Flop d_ff_3 (.clk(clock_1_out), .D(demultiplexer_1_out0[1]), .Q(d_ff_4_q[1]));  // open: Qn, preset, en, reset
  D_Flip_Flop d_ff_4 (.clk(clock_1_out), .D(demultiplexer_1_out0[0]), .Q(d_ff_4_q[0]));  // open: Qn, preset, en, reset
  Demultiplexer #(.width(2), .tristate("true"), .enable("false")) demultiplexer_1 (
    .out0(demultiplexer_1_out0), .out1(demultiplexer_1_out1), .in(multiplexer_3_out), .sel(dest_reg));
  Multiplexer #(.select(2), .width(2), .enable("false")) multiplexer_3 (
    .in0(d_ff_4_q), .in1(d_ff_2_q), .in2(imm_operand), .in3(n2_bit_alu_1_d0), .out(multiplexer_3_out),
    .sel(result_source));

  // Notes on the sheet:
  //   2-bit CPU, version 4
  //   Reg1
  //   ALU Instructions:
  //   00 = ADD A
  //   01 = A AND B
  //   10 = A OR B
  //   11 = NOT
  //   A1 A0
  //   D1D0
  //   Reg0
  //   B1B0
  //   2-bit ALU
endmodule

module _2_bit_ALU (
  input  f0,
  input  A1,
  input  A0,
  input  B1,
  input  B0,
  input  f1,
  output cout,
  output D1,
  output D0
);

  wire and_1_out, and_2_out, and_3_out, and_4_out, and_5_out, and_6_out, and_7_out, and_8_out, and_9_out,
       and_10_out, and_11_out, and_12_out, and_13_out, and_14_out, and_15_out, and_16_out, and_17_out,
       not_1_out, not_2_out, or_2_out, or_4_out, xor_1_out, xor_2_out, xor_3_out;

  and and_1 (and_1_out, ~f0, ~f1);  // AND_Gate
  and and_2 (and_2_out, f0, ~f1);  // AND_Gate
  and and_3 (and_3_out, ~f0, f1);  // AND_Gate
  and and_4 (and_4_out, f0, f1);
  or or_1 (cout, and_5_out, and_6_out);
  and and_5 (and_5_out, and_1_out, B1, A1);
  xor xor_1 (xor_1_out, A1, B1);
  and and_6 (and_6_out, and_1_out, and_12_out, xor_1_out);
  xor xor_2 (xor_2_out, xor_1_out, and_12_out);
  or or_2 (or_2_out, A1, B1);
  and and_7 (and_7_out, A1, B1);
  and and_8 (and_8_out, and_7_out, and_2_out);
  and and_9 (and_9_out, xor_2_out, and_1_out);
  or or_3 (D1, and_9_out, and_8_out, and_11_out, and_10_out);
  not not_1 (not_1_out, A1);
  and and_10 (and_10_out, not_1_out, and_4_out);
  and and_11 (and_11_out, or_2_out, and_3_out);
  and and_12 (and_12_out, and_1_out, B0, A0);
  xor xor_3 (xor_3_out, A0, B0);
  and and_13 (and_13_out, xor_3_out, and_1_out);
  or or_4 (or_4_out, A0, B0);
  and and_14 (and_14_out, A0, B0);
  and and_15 (and_15_out, or_4_out, and_3_out);
  and and_16 (and_16_out, and_14_out, and_2_out);
  or or_5 (D0, and_13_out, and_16_out, and_15_out, and_17_out);
  not not_2 (not_2_out, A0);
  and and_17 (and_17_out, not_2_out, and_4_out);

  // Notes on the sheet:
  //   Instructions:
  //   00 = ADD A
  //   01 = A AND B
  //   10 = A OR B
  //   11 = NOT
  //   A 2-bit
  //   Arithmetic Logic Unit
  //   (ALU)
  //   decoder
  //   full-
  //   adder
  //   carry
  //   half-
  //   adder
endmodule
