// Logisim project 2-bit CPU v6.circ as structural Verilog: 3 circuits, main circuit main
module main (
  input  [7:0] in_1,
  output cout
);

  wire clock_1_out, Instr__Decode_alu_instruction, Instr__Decode_dest_mux, Instr__Decode_out_2;
  wire [1:0] d_ff_2_q, d_ff_4_q, demultiplexer_1_out0, demultiplexer_1_out1, Instr__Decode_alu_a,
       Instr__Decode_alu_b, Instr__Decode_imm, Instr__Decode_result_mux, multiplexer_1_out,
       multiplexer_2_out, multiplexer_3_out, n2_bit_alu_1_d0, undriven, undriven_2;

  Clock clock_1 (.out(clock_1_out));
  Instruction_Decoder Instr__Decode (
    .in_1(in_1), .out_2(Instr__Decode_out_2), .ALU_Instruction(Instr__Decode_alu_instruction),
    .ALU_A(Instr__Decode_alu_a), .ALU_B(Instr__Decode_alu_b), .imm(Instr__Decode_imm),
    .result_mux(Instr__Decode_result_mux), .dest_mux(Instr__Decode_dest_mux));
  D_Flip_Flop d_ff_1 (.clk(clock_1_out), .D(demultiplexer_1_out1[1]), .Q(d_ff_2_q[1]));  // open: Qn, preset, en, reset
  D_Flip_Flop d_ff_2 (.clk(clock_1_out), .D(demultiplexer_1_out1[0]), .Q(d_ff_2_q[0]));  // open: Qn, preset, en, reset
  Multiplexer #(.select(2), .width(2), .enable("false")) multiplexer_1 (
    .in0(d_ff_4_q), .in1(d_ff_2_q), .in2(Instr__Decode_imm), .in3(undriven), .out(multiplexer_1_out),
    .sel(Instr__Decode_alu_a));
  Multiplexer #(.select(2), .width(2), .enable("false")) multiplexer_2 (
    .in0(d_ff_4_q), .in1(d_ff_2_q), .in2(Instr__Decode_imm), .in3(undriven_2), .out(multiplexer_2_out),
    .sel(Instr__Decode_alu_b));
  _2_bit_ALU u_2_bit_alu_1 (
    .f0(Instr__Decode_out_2), .f1(Instr__Decode_alu_instruction), .cout(cout), .B0(multiplexer_2_out[0]),
    .B1(multiplexer_2_out[1]), .A0(multiplexer_1_out[0]), .A1(multiplexer_1_out[1]), .D1(n2_bit_alu_1_d0[1]),
    .D0(n2_bit_alu_1_d0[0]));
  // Probe on Instr__Decode_out_2
  // Probe on Instr__Decode_alu_instruction
  D_Flip_Flop d_ff_3 (.clk(clock_1_out), .D(demultiplexer_1_out0[1]), .Q(d_ff_4_q[1]));  // open: Qn, preset, en, reset
  // Probe on Instr__Decode_alu_a
  // Probe on Instr__Decode_alu_b
  D_Flip_Flop d_ff_4 (.clk(clock_1_out), .D(demultiplexer_1_out0[0]), .Q(d_ff_4_q[0]));  // open: Qn, preset, en, reset
  // Probe on Instr__Decode_imm
  Demultiplexer #(.width(2), .tristate("true"), .enable("false")) demultiplexer_1 (
    .out0(demultiplexer_1_out0), .out1(demultiplexer_1_out1), .in(multiplexer_3_out),
    .sel(Instr__Decode_dest_mux));
  Multiplexer #(.select(2), .width(2), .enable("false")) multiplexer_3 (
    .in0(d_ff_4_q), .in1(d_ff_2_q), .in2(Instr__Decode_imm), .in3(n2_bit_alu_1_d0), .out(multiplexer_3_out),
    .sel(Instr__Decode_result_mux));
  // Probe on Instr__Decode_result_mux
  // Probe on Instr__Decode_dest_mux

  // Notes on the sheet:
  //   2-bit CPU, version 6
  //   Reg1
  //   ALU Instructions:
  //   00 = ADD A
  //   01 = A AND B
  //   10 = A OR B
  //   11 = NOT
  //   A1 A0
  //   B1B0
  //   2-bit ALU
  //   D1D0
  //   ALU inst
  //   Reg0
  //   ALU B
  //   ALU A
  //   ALU MUX
  //   00=Reg0  01=Reg1
  //   10=imm  11=xx
  //   imm
  //   Res MUX
  //   dest
  //   RES MUX
  //   00=Reg0  01=Reg1
  //   10=imm  11=ALU
endmodule

module _2_bit_ALU (
  input  f0,
  input  A1,
  input  A0,
  input  B1,
  input  B0,
  input  f1,
  output cout,
  output D1,
  output D0
);

  wire and_1_out, and_2_out, and_3_out, and_4_out, and_5_out, and_6_out, and_7_out, and_8_out, and_9_out,
       and_10_out, and_11_out, and_12_out, and_13_out, and_14_out, and_15_out, and_16_out, and_17_out,
       not_1_out, not_2_out, or_2_out, or_4_out, xor_1_out, xor_2_out, xor_3_out;

  and and_1 (and_1_out, ~f0, ~f1);  // AND_Gate
  and and_2 (and_2_out, f0, ~f1);  // AND_Gate
  and and_3 (and_3_out, ~f0, f1);  // AND_Gate
  and and_4 (and_4_out, f0, f1);
  or or_1 (cout, and_5_out, and_6_out);
  and and_5 (and_5_out, and_1_out, B1, A1);
  xor xor_1 (xor_1_out, A1, B1);
  and and_6 (and_6_out, and_1_out, and_12_out, xor_1_out);
  xor xor_2 (xor_2_out, xor_1_out, and_12_out);
  and and_7 (and_7_out, A1, B1);
  or or_2 (or_2_out, A1, B1);
  and and_8 (and_8_out, and_7_out, and_2_out);
  and and_9 (and_9_out, xor_2_out, and_1_out);
  or or_3 (D1, and_9_out, and_8_out, and_10_out, and_11_out);
  not not_1 (not_1_out, A1);
  and and_10 (and_10_out, or_2_out, and_3_out);
  and and_11 (and_11_out, not_1_out, and_4_out);
  and and_12 (and_12_out, and_1_out, B0, A0);
  xor xor_3 (xor_3_out, A0, B0);
  and and_13 (and_13_out, xor_3_out, and_1_out);
  and and_14 (and_14_out, A0, B0);
  or or_4 (or_4_out, A0, B0);
  and and_15 (and_15_out, and_14_out, and_2_out);
  and and_16 (and_16_out, or_4_out, and_3_out);
  or or_5 (D0, and_13_out, and_15_out, and_16_out, and_17_out);
  not not_2 (not_2_out, A0);
  and and_17 (and_17_out, not_2_out, and_4_out);

  // Notes on the sheet:
  //   Instructions:
  //   00 = ADD A
  //   01 = A AND B
  //   10 = A OR B
  //   11 = NOT
  //   A 2-bit
  //   Arithmetic Logic Unit
  //   (ALU)
  //   decoder
  //   full-
  //   adder
  //   carry
  //   half-
  //   adder
endmodule

module Instruction_Decoder (
  input  [7:0] in_1,
  output out_2,
  output ALU_Instruction,
  output [1:0] ALU_A,
  output [1:0] ALU_B,
  output [1:0] imm,
  output [1:0] result_mux,
  output dest_mux
);

  wire and_2_out;

  and and_1 (ALU_B[0], ~in_1[3], in_1[2]);  // AND_Gate
  and and_2 (and_2_out, ~in_1[3], in_1[2]);  // AND_Gate
  or or_1 (result_mux[1], ~in_1[7], in_1[3]);  // OR_Gate
  or or_2 (result_mux[0], ~in_1[7], and_2_out);  // OR_Gate

  assign ALU_A = {1'b0, in_1[4]};
  assign ALU_B[1] = in_1[3];
  assign ALU_Instruction = in_1[6];
  assign dest_mux = in_1[0];
  assign imm = in_1[2:1];
  assign out_2 = in_1[5];

  // Notes on the sheet:
  //   Instruction Decoder
endmodule
